// Logisim project ALU.circ as structural Verilog: 3 circuits, main circuit main
module main (
  input  [7:0] in_1,
  input  [7:0] in_2,
  input  [3:0] in_3,
  output [7:0] out_4
);

  ALU alu_1 (.X(in_1), .Y(in_2), .in_3(in_3), .out_4(out_4));
endmodule

module CMP (
  input  [7:0] X,
  input  [7:0] Y,
  output [7:0] out_3
);

  wire comparator_1_eq;

  Comparator comparator_1 (.a(X), .b(Y), .eq(comparator_1_eq));  // open: gt, lt
  Multiplexer #(.width(8)) multiplexer_1 (
    .in0({8{1'b1}}), .in1({8{1'b0}}), .out(out_3), .sel(comparator_1_eq));  // open: en
endmodule

module ALU (
  input  [7:0] X,
  input  [7:0] Y,
  input  [3:0] in_3,
  output [7:0] out_4
);

  wire [7:0] adder_1_out, and_1_out, CMP_out_3, divider_1_out, divider_1_rem, multiplier_1_out, not_1_out,
       or_1_out, shifter_1_out, shifter_2_out, shifter_3_out, shifter_4_out, subtractor_1_out, xor_1_out;

  CMP CMP (.X(X), .Y(Y), .out_3(CMP_out_3));
  assign not_1_out = ~X;  // NOT_Gate not_1, 8 bits wide
  assign and_1_out = X & Y;  // AND_Gate and_1, 8 bits wide
  assign or_1_out = X | Y;  // OR_Gate or_1, 8 bits wide
  assign xor_1_out = X ^ Y;  // XOR_Gate xor_1, 8 bits wide
  Shifter #(.shift("lr")) shifter_1 (.in(X), .\dist (3'b001), .out(shifter_1_out));
  Shifter shifter_2 (.in(X), .\dist (3'b001), .out(shifter_2_out));
  Shifter #(.shift("rr")) shifter_3 (.in(X), .\dist (3'b001), .out(shifter_3_out));
  Shifter #(.shift("rl")) shifter_4 (.in(X), .\dist (3'b001), .out(shifter_4_out));
  Adder adder_1 (.a(X), .b(Y), .out(adder_1_out));  // open: cin, cout
  Subtractor subtractor_1 (.a(X), .b(Y), .out(subtractor_1_out));  // open: bin, bout
  Multiplier multiplier_1 (.a(X), .b(Y), .out(multiplier_1_out));  // open: cin, cout
  Divider divider_1 (.a(X), .b(Y), .out(divider_1_out), .rem(divider_1_rem));  // open: upper
  Multiplexer #(.select(4), .width(8)) multiplexer_1 (
    .in0({8{1'b0}}), .in1(adder_1_out), .in2(subtractor_1_out), .in3(multiplier_1_out), .in4(divider_1_out),
    .in5(divider_1_rem), .in6(CMP_out_3), .in7(not_1_out), .in8(and_1_out), .in9(or_1_out), .in10(xor_1_out),
    .in11(shifter_1_out), .in12(shifter_2_out), .in13(shifter_3_out), .in14(shifter_4_out), .in15({8{1'b1}}),
    .out(out_4), .sel(in_3));  // open: en
endmodule
