// Logisim project CU.circ as structural Verilog: 2 circuits, main circuit main
// CU
module main (
  input  [15:0] Instruction,
  output [3:0] COM,
  output [2:0] A1,
  output [2:0] A2,
  output [2:0] A3,
  output [7:0] MA
);

  wire C1, not_1_out;
  wire [7:0] parser_1_m1, parser_1_m2;

  PARSER parser_1 (
    .Instruction(Instruction), .COMMAND(COM), .A1(A1), .A2(A2), .A3(A3), .M1(parser_1_m1), .M2(parser_1_m2));
  Multiplexer #(.width(8)) multiplexer_1 (.in0(parser_1_m1), .in1(parser_1_m2), .out(MA), .sel(C1));  // open: en
  not not_1 (not_1_out, COM[0]);
  and and_1 (C1, not_1_out, COM[1]);
endmodule

// PAR
module PARSER (
  input  [15:0] Instruction,
  output [3:0] COMMAND,
  output [2:0] A1,
  output [2:0] A2,
  output [2:0] A3,
  output [7:0] M1,
  output [7:0] M2
);


  assign A1 = Instruction[6:4];
  assign A2 = Instruction[9:7];
  assign A3 = Instruction[12:10];
  assign COMMAND = Instruction[3:0];
  assign M1 = Instruction[11:4];
  assign M2 = Instruction[14:7];
endmodule
